# Fritzing sketch example_button (saved by Fritzing 0.9.2b)

parts:
  U1 = ESP8266 WiFi Module [part_number=ESP8266]
  VCC1 = Battery
  S1 = Round Pushbutton
  R1 = Resistor [tolerance=±5% resistance=220 package=THT]

nets:
  N1: U1.VCC, U1.CH_PD, VCC1.+, R1.Pin_1
  N2: U1.GPIO_2, S1.leg0, R1.Pin_0
  N3: U1.GND, VCC1.-, S1.leg1

custom parts:
  ESP8266 WiFi Module: Generic WiFi Module based on the ESP8266 with onboard PCB antenna and UART communications
