# Fritzing sketch example_led (saved by Fritzing 0.9.2b)

parts:
  U1 = ESP8266 WiFi Module [part_number=ESP8266]
  VCC1 = Battery
  R1 = Resistor [tolerance=±5% resistance=220 package=THT]
  LED1 = LED - 5mm [color="Red (633nm)" package="5 mm [THT]"]

nets:
  N1: U1.VCC, U1.CH_PD
  N2: U1.GPIO_2, R1.Pin_0
  N3: U1.GND, VCC1.-, LED1.anode
  N4: R1.Pin_1, LED1.cathode

custom parts:
  ESP8266 WiFi Module: Generic WiFi Module based on the ESP8266 with onboard PCB antenna and UART communications
